// Logisim project Pipelined_Processor.circ as structural Verilog: 1 circuit, main circuit main
module main (
  input  clear,
  input  clear_2
);

  wire AluSrc, clk, ExtOp, Kill1, main_2_p1, main_2_p4, main_4_p5, MemRd, MemWr, RegWr, zero_flag;
  wire [1:0] ForwardA, ForwardB, func, PCSrc, RegDst, WBdata;
  wire [2:0] main_4_p6, main_4_p7, multiplexer_2_out, RD2_q, RD3_q;
  wire [4:0] imm5, op;
  wire [10:0] imm11, register_2_q, register_3_q;
  wire [12:0] AluOp;
  wire [15:0] multiplexer_1_out, register_1_q, rom_1_data;
  wire [19:0] main_1_p3;
  wire [31:0] ALU, BusA, BusB, D_q, ExtImm5, Imm_q, main_6_p8, main_6_p9, main_9_p6, MEM, multiplexer_3_out,
       multiplexer_4_out, multiplexer_5_out, PC___2, R_q, WB;

  // PC_Register_main main_1: pin names not known; wires that end beside it: imm5, imm11, main_1_p3, BusA, PCSrc, clk, clear, main_1_p3
  ROM #(.addrWidth(20), .dataWidth(16)) rom_1 (.addr(main_1_p3), .data(rom_1_data), .sel(1'b1));
  // PCControl_main main_2: pin names not known; wires that end beside it: main_2_p1, op, zero_flag, main_2_p4, main_2_p1, main_2_p4, PCSrc
  // ALUControl_main main_3: pin names not known; wires that end beside it: func, op, AluOp
  Clock clock_1 (.out(clk));
  Multiplexer #(.width(16), .enable("false")) multiplexer_1 (
    .in0(rom_1_data), .in1({16{1'b0}}), .out(multiplexer_1_out), .sel(Kill1));
  assign PC___2 = {{12{1'b0}}, main_1_p3};  // Bit_Extender bit_extender_1
  Register #(.width(16)) register_1 (.D(multiplexer_1_out), .Q(register_1_q), .clk(clk));  // open: en, clr
  // InstractionDecoder_main main_4: pin names not known; wires that end beside it: register_1_q, imm5, imm11, op, main_4_p5, main_4_p6, main_4_p7, func
  // MainControl_main main_5: pin names not known; wires that end beside it: op, WBdata, MemWr, MemRd, AluSrc, ExtOp, RegWr, RegDst
  Multiplexer #(.select(2), .width(3), .enable("false")) multiplexer_2 (
    .in0(main_4_p6), .in1(main_4_p7), .in2(3'b111), .in3(3'b000), .out(multiplexer_2_out), .sel(RegDst));
  // RegisterFile_main main_6: pin names not known; wires that end beside it: main_4_p5, main_4_p6, multiplexer_2_out, RegWr, clk, clear_2, WB, main_6_p8, main_6_p9
  Multiplexer #(.select(2), .width(32), .enable("false")) multiplexer_3 (
    .in0(main_6_p8), .in1(ALU), .in2(MEM), .in3(WB), .out(multiplexer_3_out), .sel(ForwardA));
  Multiplexer #(.select(2), .width(32), .enable("false")) multiplexer_4 (
    .in0(main_6_p9), .in1(ALU), .in2(MEM), .in3(WB), .out(multiplexer_4_out), .sel(ForwardB));
  Register #(.width(32)) A (.D(multiplexer_3_out), .en(1'b1), .Q(BusA), .clk(clk));  // open: clr
  Register #(.width(32)) B (.D(multiplexer_4_out), .en(1'b1), .Q(BusB), .clk(clk));  // open: clr
  Register #(.width(3)) RD2 (.D(multiplexer_2_out), .en(1'b1), .Q(RD2_q), .clk(clk));  // open: clr
  Register #(.width(11)) register_2 (.Q(register_2_q), .clk(clk));  // open: D, en, clr
  Register #(.width(32)) Imm (.D(ExtImm5), .en(1'b1), .Q(Imm_q), .clk(clk));  // open: clr
  Multiplexer #(.width(32), .enable("false")) multiplexer_5 (
    .in0(BusB), .in1(Imm_q), .out(multiplexer_5_out), .sel(AluSrc));
  // ALU_main main_7: pin names not known; wires that end beside it: BusA, multiplexer_5_out, zero_flag, AluOp, ALU
  Register #(.width(32)) R (.D(ALU), .en(1'b1), .Q(R_q), .clk(clk));  // open: clr
  Register #(.width(32)) D (.D(BusB), .en(1'b1), .Q(D_q), .clk(clk));  // open: clr
  Register #(.width(3)) RD3 (.D(RD2_q), .en(1'b1), .Q(RD3_q), .clk(clk));  // open: clr
  Register #(.width(11)) register_3 (.D(register_2_q), .en(register_2_q[0]), .Q(register_3_q), .clk(clk));  // open: clr
  // Extender_main main_8: pin names not known; wires that end beside it: imm5, ExtOp, ExtImm5
  // DataMemory_main main_9: pin names not known; wires that end beside it: R_q[19:0], D_q, clk, MemWr, MemRd, main_9_p6, RD3_q
  Multiplexer #(.select(2), .width(32), .enable("false")) multiplexer_6 (
    .in0(ALU), .in1(main_9_p6), .in2(PC___2), .in3({32{1'b0}}), .out(MEM), .sel(WBdata));
  Register #(.width(32)) register_4 (.D(MEM), .en(1'b1), .Q(WB));  // open: clk, clr
  Register #(.width(3)) RD4 (.D(RD3_q), .clk(clk));  // open: en, Q, clr
  Register #(.width(11)) register_5 (.D(register_3_q), .clk(clk));  // open: en, Q, clr
  // Pins of 1 and 11 bits meet at register_2_q

  // Notes on the sheet:
  //   contents of rom_1 (hex, n*v repeats v):
  //   4025
endmodule
