// Logisim project Single_Cycle_CPU.circ as structural Verilog: 1 circuit, main circuit main
module main (
  input  clear
);

  wire AluSrc, clk, ExtOp, main_3_p5, MemRd, MemWr, RegWr, zero_flag;
  wire [1:0] func, PCSrc, RegDst, WBdata;
  wire [2:0] main_3_p6, main_3_p7, multiplexer_1_out;
  wire [4:0] imm5, op;
  wire [10:0] imm11;
  wire [12:0] AluOp;
  wire [15:0] rom_1_data;
  wire [19:0] main_1_p3;
  wire [31:0] ALU_Result, bit_extender_1_out, BusA, BusB, BusW, ExtImm5, main_9_p6, multiplexer_2_out, PC___1;

  // PC_Register_main main_1: pin names not known; wires that end beside it: imm5, imm11, main_1_p3, BusA, PCSrc, clk, clear, main_1_p3
  assign bit_extender_1_out = {{12{1'b0}}, main_1_p3};  // Bit_Extender bit_extender_1
  ROM #(.addrWidth(20), .dataWidth(16)) rom_1 (.addr(main_1_p3), .data(rom_1_data), .sel(1'b1));
  Adder #(.width(32)) adder_1 (.a(32'h1), .b(bit_extender_1_out), .out(PC___1), .cin(1'b0));  // open: cout
  // PCControl_main main_2: pin names not known; wires that end beside it: op, zero_flag, PCSrc, op
  Clock clock_1 (.out(clk));
  // InstractionDecoder_main main_3: pin names not known; wires that end beside it: rom_1_data, imm5, imm11, op, main_3_p5, main_3_p6, main_3_p7, func
  Multiplexer #(.select(2), .width(3), .enable("false")) multiplexer_1 (
    .in0(main_3_p6), .in1(main_3_p7), .in2(3'b111), .in3(3'b000), .out(multiplexer_1_out), .sel(RegDst));
  // MainControl_main main_4: pin names not known; wires that end beside it: WBdata, MemWr, MemRd, AluSrc, ExtOp, RegWr, RegDst
  // RegisterFile_main main_5: pin names not known; wires that end beside it: main_3_p5, main_3_p6, multiplexer_1_out, RegWr, clk, clear, BusW, BusA, BusB
  Multiplexer #(.width(32), .enable("false")) multiplexer_2 (
    .in0(BusB), .in1(ExtImm5), .out(multiplexer_2_out), .sel(AluSrc));
  // ALU_main main_6: pin names not known; wires that end beside it: BusA, multiplexer_2_out, zero_flag, AluOp, ALU_Result
  // Extender_main main_7: pin names not known; wires that end beside it: imm5, ExtOp, ExtImm5
  // ALUControl_main main_8: pin names not known; wires that end beside it: func, op, AluOp
  // DataMemory_main main_9: pin names not known; wires that end beside it: ALU_Result[19:0], BusB, clk, MemWr, MemRd, main_9_p6
  Multiplexer #(.select(2), .width(32), .enable("false")) multiplexer_3 (
    .in0(ALU_Result), .in1(main_9_p6), .in2(PC___1), .in3({32{1'b0}}), .out(BusW), .sel(WBdata));

  // Notes on the sheet:
  //   contents of rom_1 (hex, n*v repeats v):
  //   3023 30e7 2967 2145 3986 45cd 4b8a 54af 5e6e 270 73d 18e 14f 94c 975 c7a a77 8544 0 0 0 8d44 92a6
  //   9be2 0 ad80 a862 a520 d940
endmodule
